# Fritzing sketch FisPlusColor (saved by Fritzing 0.9.3b)
breadboards: 1

parts:
  TFT1 = 2.2" TFT with MicroSD Breakout
  Composant1 = Arduino Pro Mini (3.3V)
  Power_plug1 = Power plug
  Composant2 = BluePill
  TFT2 = 2.2" TFT with MicroSD Breakout
  Power_plug2 = Power plug

nets:
  N1: TFT1.CS, Composant1.D10
  N2: TFT1.RST, Composant1.D8
  VCC: TFT1.VIN, Composant1.VCC, Power_plug1.VCC
  GND: TFT1.GND, Composant1.GND, Power_plug1.GND
  VIN: Composant2.VBAT, TFT2.VIN, Power_plug2.VCC
  N3: Composant2.A0, TFT2.CS
  N4: Composant2.A1, TFT2.RST
  N5: Composant2.A5, TFT2.SCK
  N6: Composant2.A7, TFT2.SDCS
  GND_2: Composant2.GND3, TFT2.GND, Power_plug2.GND

custom parts:
  2.2" TFT with MicroSD Breakout: 2.2" TFT Display with HX8340B Controller and MicroSD Card
